// Logisim project 171044073.circ as structural Verilog: 10 circuits, main circuit main
module main (
  input  re_start,
  input  score_clear,
  output [7:0] out_3,
  output [7:0] out_4,
  output [2:0] counter,
  output [7:0] out_6,
  output [7:0] out_7,
  output [7:0] out_8,
  output [7:0] out_9,
  output [7:0] out_10,
  output [7:0] out_11,
  output [7:0] out_12,
  output [2:0] out_13
);

  wire A_out, B_out, C_out, clock_1_out, control_unit_1_dec, control_unit_1_letreg, control_unit_1_reg,
       control_unit_1_regtty, D_out, datapath_1_false, datapath_1_tr, decoder_display_1_a_2,
       decoder_display_1_b_2, decoder_display_1_c_2, decoder_display_1_d_2, decoder_display_1_e,
       decoder_display_1_f, decoder_display_1_g, display_1_eq7num, E_out, F_out, G_out, H_out, I_out, J_out,
       K_out, L_out, M_out, matris_1_dead, not_1_out, score_decoder_1_a_2, score_decoder_1_b_2,
       score_decoder_1_c_2, score_decoder_1_d_2, score_decoder_1_e, score_decoder_1_f, score_decoder_1_g,
       score_decoder_2_a_2, score_decoder_2_b_2, score_decoder_2_c_2, score_decoder_2_d_2, score_decoder_2_e,
       score_decoder_2_f, score_decoder_2_g;
  wire [3:0] display_1_numlet, score_table_1_nuumber, score_table_2_nuumber;
  wire [6:0] bit_extender_1_out, matris_1_n0, matris_1_n1, matris_1_n2, matris_1_n3, matris_1_n4;
  wire [7:0] datapath_1_register_tty_2, display_1_let1r, display_1_let2r, display_1_let3r, display_1_let4r,
       display_1_let5r, display_1_let6r, display_1_let7r, display_1_let8r;
  wire [12:0] N_out;

  _7_Segment_Display u_7_segment_display_1 (
    .g(score_decoder_1_g), .f(score_decoder_1_f), .a(score_decoder_1_a_2), .b(score_decoder_1_b_2),
    .e(score_decoder_1_e), .d(score_decoder_1_d_2), .c(score_decoder_1_c_2));  // open: dp
  Clock clock_1 (.out(clock_1_out));
  score_decoder score_decoder_1 (
    .d(score_table_1_nuumber[3]), .c(score_table_1_nuumber[2]), .b(score_table_1_nuumber[1]),
    .a(score_table_1_nuumber[0]), .clock(clock_1_out), .score_clear(score_clear), .a_2(score_decoder_1_a_2),
    .b_2(score_decoder_1_b_2), .c_2(score_decoder_1_c_2), .d_2(score_decoder_1_d_2), .e(score_decoder_1_e),
    .f(score_decoder_1_f), .g(score_decoder_1_g));  // open: decoder_enable
  _7_Segment_Display u_7_segment_display_2 (
    .g(score_decoder_2_g), .f(score_decoder_2_f), .a(score_decoder_2_a_2), .b(score_decoder_2_b_2),
    .e(score_decoder_2_e), .d(score_decoder_2_d_2), .c(score_decoder_2_c_2));  // open: dp
  score_table score_table_1 (
    .Cu(out_13), .fls(not_1_out), .score_clear(score_clear), .clock(clock_1_out),
    .nuumber(score_table_1_nuumber));
  score_decoder score_decoder_2 (
    .d(score_table_2_nuumber[3]), .c(score_table_2_nuumber[2]), .b(score_table_2_nuumber[1]),
    .a(score_table_2_nuumber[0]), .clock(clock_1_out), .score_clear(score_clear), .a_2(score_decoder_2_a_2),
    .b_2(score_decoder_2_b_2), .c_2(score_decoder_2_c_2), .d_2(score_decoder_2_d_2), .e(score_decoder_2_e),
    .f(score_decoder_2_f), .g(score_decoder_2_g));  // open: decoder_enable
  rom rom_1 (
    .Clock(clock_1_out), .random_enable(re_start), .N1(out_3), .N2(out_4), .N3(out_6), .N4(out_7),
    .N5(out_8), .N6(out_9), .N7(out_10), .N8(out_11));
  not not_1 (not_1_out, matris_1_dead);
  control_unit control_unit_1 (
    .l7(display_1_eq7num), .true(datapath_1_tr), .dead(matris_1_dead), .clock(clock_1_out), .clear(re_start),
    .dec(control_unit_1_dec), .\reg (control_unit_1_reg), .letreg(control_unit_1_letreg),
    .regtty(control_unit_1_regtty), .cul2(out_13[2]), .cu1(out_13[1]), .cu0(out_13[0]));
  score_table score_table_2 (
    .Cu(out_13), .fls(matris_1_dead), .score_clear(score_clear), .clock(clock_1_out),
    .nuumber(score_table_2_nuumber));
  Button A (.out(A_out));
  Button B (.out(B_out));
  Button C (.out(C_out));
  Button D (.out(D_out));
  Button E (.out(E_out));
  Button F (.out(F_out));
  Button G (.out(G_out));
  Button H (.out(H_out));
  Button I (.out(I_out));
  Button J (.out(J_out));
  Button K (.out(K_out));
  Button L (.out(L_out));
  Button M (.out(M_out));
  display display_1 (
    .let1(out_3), .let2(out_4), .let3(out_6), .let4(out_7), .let5(out_8), .let6(out_9), .let7(out_10),
    .let8(out_11), .clock(clock_1_out), .clear(re_start), .register_enable(control_unit_1_reg),
    .letregister(control_unit_1_letreg), .numlet(display_1_numlet), .counter(counter),
    .eq7num(display_1_eq7num), .let1r(display_1_let1r), .let2r(display_1_let2r), .let3r(display_1_let3r),
    .let4r(display_1_let4r), .let5r(display_1_let5r), .let6r(display_1_let6r), .let7r(display_1_let7r),
    .let8r(display_1_let8r));
  datapath datapath_1 (
    .let1(display_1_let1r), .let2(display_1_let2r), .let3(display_1_let3r), .let4(display_1_let4r),
    .let5(display_1_let5r), .let6(display_1_let6r), .let7(display_1_let7r), .let8(display_1_let8r),
    .clear(re_start), .keybord(out_12), .clock(clock_1_out), .cu_letl(out_13),
    .register_tty(control_unit_1_regtty), .tr(datapath_1_tr), .register_tty_2(datapath_1_register_tty_2),
    .false(datapath_1_false));
  keybord keybord_1 (
    .A(A_out), .B(B_out), .C(C_out), .D(D_out), .E(E_out), .F(F_out), .G(G_out), .H(H_out), .I(I_out),
    .J(J_out), .K(K_out), .L(L_out), .M(M_out), .N(N_out[0]), .O(N_out[1]), .P(N_out[2]), .Q(N_out[3]),
    .R(N_out[4]), .S(N_out[5]), .T(N_out[6]), .U(N_out[7]), .V(N_out[8]), .W(N_out[9]), .X(N_out[10]),
    .Y(N_out[11]), .Z(N_out[12]), .N7(out_12[7]), .N6(out_12[6]), .N5(out_12[5]), .N4(out_12[4]),
    .N3(out_12[3]), .N2(out_12[2]), .N1(out_12[1]), .N0(out_12[0]));
  decoder_display decoder_display_1 (
    .d(display_1_numlet[3]), .c(display_1_numlet[2]), .b(display_1_numlet[1]), .a(display_1_numlet[0]),
    .decoder_enable(control_unit_1_dec), .clock(clock_1_out), .a_2(decoder_display_1_a_2),
    .b_2(decoder_display_1_b_2), .c_2(decoder_display_1_c_2), .d_2(decoder_display_1_d_2),
    .e(decoder_display_1_e), .f(decoder_display_1_f), .g(decoder_display_1_g));
  _7_Segment_Display u_7_segment_display_3 (
    .g(decoder_display_1_g), .f(decoder_display_1_f), .a(decoder_display_1_a_2), .b(decoder_display_1_b_2),
    .e(decoder_display_1_e), .d(decoder_display_1_d_2), .c(decoder_display_1_c_2));  // open: dp
  Button N (.out(N_out[0]));
  Button O (.out(N_out[1]));
  Button P (.out(N_out[2]));
  Button Q (.out(N_out[3]));
  Button R (.out(N_out[4]));
  Button S (.out(N_out[5]));
  Button T (.out(N_out[6]));
  Button U (.out(N_out[7]));
  Button V (.out(N_out[8]));
  Button W (.out(N_out[9]));
  Button X (.out(N_out[10]));
  Button Y (.out(N_out[11]));
  Button Z (.out(N_out[12]));
  Bit_Extender #(.out_width(7)) bit_extender_1 (.in(datapath_1_register_tty_2), .out(bit_extender_1_out));
  DotMatrix dotmatrix_1 (
    .col0(matris_1_n4), .col1(matris_1_n3), .col2(matris_1_n2), .col3(matris_1_n1), .col4(matris_1_n0));
  matris matris_1 (
    .F(datapath_1_false), .clock(clock_1_out), .clear(re_start), .N4(matris_1_n4), .N3(matris_1_n3),
    .N1(matris_1_n1), .dead(matris_1_dead), .N2(matris_1_n2), .N0(matris_1_n0));
  TTY #(.rows(4), .cols(10)) tty_1 (.data(bit_extender_1_out), .clk(clock_1_out), .clr(re_start));  // open: we

  // Notes on the sheet:
  //   COMPUTER
  //   PERSON
endmodule

module display (
  input  [7:0] let1,
  input  [7:0] let2,
  input  [7:0] let3,
  input  [7:0] let4,
  input  [7:0] let5,
  input  [7:0] let6,
  input  [7:0] let7,
  input  [7:0] let8,
  input  clock,
  input  clear,
  input  register_enable,
  input  letregister,
  output [3:0] numlet,
  output [2:0] counter,
  output eq7num,
  output [7:0] let1r,
  output [7:0] let2r,
  output [7:0] let3r,
  output [7:0] let4r,
  output [7:0] let5r,
  output [7:0] let6r,
  output [7:0] let7r,
  output [7:0] let8r
);

  wire comparator_1_gt, comparator_1_lt, comparator_2_eq, not_1_out, not_2_out, not_3_out, or_1_out;
  wire [1:0] and_1_out, register_9_q;
  wire [3:0] adder_1_out, bit_extender_1_out;
  wire [7:0] multiplexer_1_out;

  Counter #(.width(3), .max('h7)) counter_1 (
    .D(3'b000), .Q(counter), .clk(clock), .clr(clear));  // open: load, count, carry
  Register register_1 (.D(let1), .Q(let1r), .clk(clock));  // open: en, clr
  Register register_2 (.D(let2), .en(letregister), .Q(let2r), .clk(clock));  // open: clr
  Register register_3 (.D(let3), .en(letregister), .Q(let3r), .clk(clock));  // open: clr
  Register register_4 (.D(let4), .en(letregister), .Q(let4r), .clk(clock));  // open: clr
  Register register_5 (.D(let5), .en(letregister), .Q(let5r), .clk(clock));  // open: clr
  Register register_6 (.D(let6), .en(letregister), .Q(let6r), .clk(clock));  // open: clr
  Register register_7 (.D(let7), .en(letregister), .Q(let7r), .clk(clock));  // open: clr
  Register register_8 (.D(let8), .en(letregister), .Q(let8r), .clk(clock));  // open: clr
  Multiplexer #(.select(3), .width(8)) multiplexer_1 (
    .in0(let1), .in1(let2), .in2(let3), .in3(let4), .in4(let5), .in5(let6), .in6(let7), .in7(let8),
    .out(multiplexer_1_out), .sel(counter));  // open: en
  Comparator comparator_1 (
    .a(multiplexer_1_out), .b({8{1'b0}}), .gt(comparator_1_gt), .lt(comparator_1_lt));  // open: eq
  Comparator #(.width(3)) comparator_2 (.a(3'b111), .b(counter), .eq(comparator_2_eq));  // open: gt, lt
  or or_1 (or_1_out, comparator_1_gt, comparator_1_lt);
  not not_1 (not_1_out, register_9_q[1]);
  not not_2 (not_2_out, register_9_q[0]);
  not not_3 (not_3_out, register_9_q[1]);
  Register #(.width(2)) register_9 (.D(and_1_out), .Q(register_9_q), .clk(clock), .clr(clear));  // open: en
  assign bit_extender_1_out = {{3{1'b0}}, or_1_out};  // Bit_Extender bit_extender_1
  Register #(.width(4)) register_10 (.D(adder_1_out), .en(register_enable), .Q(numlet), .clk(clock), .clr(clear));
  or or_2 (and_1_out[1], register_9_q[0], register_9_q[1]);
  and and_1 (and_1_out[0], not_1_out, not_2_out, comparator_2_eq);
  and and_2 (eq7num, not_3_out, register_9_q[0]);
  Adder #(.width(4)) adder_1 (.a(bit_extender_1_out), .b(numlet), .out(adder_1_out));  // open: cin, cout
endmodule

module decoder_display (
  input  d,
  input  c,
  input  b,
  input  a,
  input  decoder_enable,
  input  clock,
  output a_2,
  output b_2,
  output c_2,
  output d_2,
  output e,
  output f,
  output g
);

  wire and_1_out, and_2_out, and_3_out, and_4_out, and_5_out, and_6_out, and_7_out, and_8_out, and_9_out,
       and_10_out, and_11_out, and_12_out, and_13_out, and_14_out, and_15_out, and_16_out, not_1_out,
       not_2_out, not_3_out, not_4_out, not_5_out, not_6_out, not_7_out, not_8_out, not_9_out, not_10_out,
       not_11_out, not_12_out, not_13_out, not_14_out, not_15_out, not_16_out, not_17_out, not_18_out,
       not_19_out, not_20_out, not_21_out;
  wire [3:0] register_1_q;

  Register #(.width(4)) register_1 (.D({a, b, c, d}), .en(decoder_enable), .Q(register_1_q), .clk(clock));  // open: clr
  not not_1 (not_1_out, register_1_q[1]);
  not not_2 (not_2_out, register_1_q[3]);
  not not_3 (not_3_out, register_1_q[2]);
  not not_4 (not_4_out, register_1_q[3]);
  not not_5 (not_5_out, register_1_q[2]);
  not not_6 (not_6_out, register_1_q[1]);
  not not_7 (not_7_out, register_1_q[3]);
  not not_8 (not_8_out, register_1_q[1]);
  not not_9 (not_9_out, register_1_q[3]);
  not not_10 (not_10_out, register_1_q[2]);
  not not_11 (not_11_out, register_1_q[1]);
  not not_12 (not_12_out, register_1_q[3]);
  not not_13 (not_13_out, register_1_q[3]);
  not not_14 (not_14_out, register_1_q[2]);
  not not_15 (not_15_out, register_1_q[3]);
  not not_16 (not_16_out, register_1_q[2]);
  not not_17 (not_17_out, register_1_q[3]);
  not not_18 (not_18_out, register_1_q[1]);
  not not_19 (not_19_out, register_1_q[2]);
  not not_20 (not_20_out, register_1_q[3]);
  and and_1 (and_1_out, not_1_out, not_2_out);
  and and_2 (and_2_out, register_1_q[1], register_1_q[3]);
  not not_21 (not_21_out, register_1_q[1]);
  and and_3 (and_3_out, not_3_out, not_4_out);
  and and_4 (and_4_out, register_1_q[2], register_1_q[3]);
  or or_1 (c_2, not_5_out, register_1_q[3], register_1_q[1]);
  and and_5 (and_5_out, not_6_out, not_7_out);
  and and_6 (and_6_out, not_8_out, register_1_q[2]);
  and and_7 (and_7_out, register_1_q[2], not_9_out);
  and and_8 (and_8_out, register_1_q[1], not_10_out, register_1_q[3]);
  and and_9 (and_9_out, not_11_out, not_12_out);
  and and_10 (and_10_out, register_1_q[2], not_13_out);
  and and_11 (and_11_out, not_14_out, not_15_out);
  and and_12 (and_12_out, register_1_q[1], not_16_out);
  and and_13 (and_13_out, register_1_q[1], not_17_out);
  and and_14 (and_14_out, not_18_out, register_1_q[2]);
  and and_15 (and_15_out, register_1_q[1], not_19_out);
  and and_16 (and_16_out, register_1_q[1], not_20_out);
  or or_2 (a_2, and_1_out, register_1_q[2], and_2_out, register_1_q[0]);
  or or_3 (b_2, not_21_out, and_3_out, and_4_out);
  or or_4 (d_2, and_5_out, and_6_out, and_7_out, and_8_out, register_1_q[0]);
  or or_5 (e, and_9_out, and_10_out);
  or or_6 (f, and_11_out, and_12_out, and_13_out, register_1_q[0]);
  or or_7 (g, and_14_out, and_15_out, and_16_out, register_1_q[0]);
endmodule

module datapath (
  input  [7:0] let1,
  input  [7:0] let2,
  input  [7:0] let3,
  input  [7:0] let4,
  input  [7:0] let5,
  input  [7:0] let6,
  input  [7:0] let7,
  input  [7:0] let8,
  input  clear,
  input  [7:0] keybord,
  input  clock,
  input  [2:0] cu_letl,
  input  register_tty,
  output tr,
  output [7:0] register_tty_2,
  output false
);

  wire and_1_out, and_4_out, comparator_1_eq, comparator_1_gt, comparator_1_lt, not_1_out, not_2_out,
       not_3_out, not_4_out, not_5_out, not_6_out, not_7_out, or_1_out;
  wire [0:0] and_2_out;
  wire [1:0] and_5_out, register_1_q, register_2_q;
  wire [7:0] multiplexer_1_out;

  Multiplexer #(.select(3), .width(8)) multiplexer_1 (
    .in0(let1), .in1(let2), .in2(let3), .in3(let4), .in4(let5), .in5(let6), .in6(let7), .in7(let8),
    .out(multiplexer_1_out), .sel(cu_letl));  // open: en
  Comparator comparator_1 (
    .a(multiplexer_1_out), .b(keybord), .gt(comparator_1_gt), .eq(comparator_1_eq), .lt(comparator_1_lt));
  and and_1 (and_1_out, let1[6], comparator_1_eq);
  Multiplexer #(.width(8)) multiplexer_2 (
    .in0({8{1'b0}}), .in1(multiplexer_1_out), .out(register_tty_2), .sel(register_tty));  // open: en
  or or_1 (or_1_out, comparator_1_gt, comparator_1_lt);
  not not_1 (not_1_out, register_1_q[1]);
  not not_2 (not_2_out, register_1_q[0]);
  not not_3 (not_3_out, register_1_q[1]);
  not not_4 (not_4_out, register_1_q[0]);
  and and_2 (and_2_out[0], not_1_out, not_2_out, and_1_out);
  and and_3 (tr, not_3_out, not_4_out, and_1_out);
  and and_4 (and_4_out, or_1_out, keybord[6]);
  Register #(.width(2)) register_1 (.D({1'b0, and_2_out[0]}), .Q(register_1_q), .clr(clear));  // open: en, clk
  and and_5 (and_5_out[0], register_2_q[1], and_4_out);
  not not_5 (not_5_out, register_2_q[1]);
  not not_6 (not_6_out, register_2_q[1]);
  not not_7 (not_7_out, register_2_q[0]);
  and and_6 (and_5_out[1], not_5_out, and_4_out);
  and and_7 (false, not_6_out, not_7_out, and_4_out);
  Register #(.width(2)) register_2 (.D(and_5_out), .en(1'b1), .Q(register_2_q), .clk(clock), .clr(clear));
endmodule

module keybord (
  input  A,
  input  B,
  input  C,
  input  D,
  input  E,
  input  F,
  input  G,
  input  H,
  input  I,
  input  J,
  input  K,
  input  L,
  input  M,
  input  N,
  input  O,
  input  P,
  input  Q,
  input  R,
  input  S,
  input  T,
  input  U,
  input  V,
  input  W,
  input  X,
  input  Y,
  input  Z,
  output N7,
  output N6,
  output N5,
  output N4,
  output N3,
  output N2,
  output N1,
  output N0
);

  wire or_1_out, or_2_out, or_3_out, or_4_out, or_5_out, or_6_out, or_7_out, or_8_out, or_9_out, or_10_out,
       or_11_out, or_12_out, or_13_out, or_14_out, or_15_out, or_16_out, or_17_out, or_18_out, or_19_out,
       or_20_out, or_21_out, or_22_out, or_23_out, or_24_out;

  or or_1 (or_1_out, E, D, C, B, A);
  or or_2 (or_2_out, E, D);
  or or_3 (or_3_out, C, B);
  or or_4 (or_4_out, E, C, A);
  or or_5 (or_5_out, J, I, H, G, F);
  or or_6 (or_6_out, J, I, H);
  or or_7 (or_7_out, G, F);
  or or_8 (or_8_out, J, G, F);
  or or_9 (or_9_out, I, G);
  or or_10 (or_10_out, O, N, M, L, K);
  or or_11 (or_11_out, O, N, M, L, K);
  or or_12 (or_12_out, O, N, M, L);
  or or_13 (or_13_out, O, N, K);
  or or_14 (or_14_out, O, M, K);
  or or_15 (or_15_out, T, S, R, Q, P);
  or or_16 (or_16_out, T, S, R, Q, P);
  or or_17 (or_17_out, S, R);
  or or_18 (or_18_out, S, Q);
  or or_19 (or_19_out, Z, Y, X, W, V, U);
  or or_20 (or_20_out, Z, Y, X, W, V, U);
  or or_21 (or_21_out, Z, Y, X);
  or or_22 (or_22_out, W, V, U);
  or or_23 (or_23_out, Z, W, V);
  or or_24 (or_24_out, Y, W, U);
  or u_N6 (N6, or_1_out, or_5_out, or_10_out, or_15_out, or_19_out);
  or u_N4 (N4, 1'b0, 1'b0, 1'b0, or_16_out, or_20_out);
  or u_N3 (N3, 1'b0, or_6_out, or_11_out, 1'b0, or_21_out);
  or u_N2 (N2, or_2_out, or_7_out, or_12_out, T, or_22_out);
  or u_N1 (N1, or_3_out, or_8_out, or_13_out, or_17_out, or_23_out);
  or u_N0 (N0, or_4_out, or_9_out, or_14_out, or_18_out, or_24_out);

  assign N5 = 1'b0;
  assign N7 = 1'b0;
endmodule

module control_unit (
  input  l7,
  input  true,
  input  dead,
  input  clock,
  input  clear,
  output dec,
  output \reg ,
  output letreg,
  output regtty,
  output cul2,
  output cu1,
  output cu0
);

  wire and_1_out, and_2_out, and_3_out, and_4_out, and_5_out, and_6_out, and_7_out, and_8_out, and_9_out,
       and_10_out, and_11_out, and_12_out, and_13_out, and_14_out, and_15_out, and_16_out, and_17_out,
       and_18_out, and_19_out, and_22_out, and_23_out, and_24_out, and_25_out, and_26_out, and_27_out,
       and_28_out, and_29_out, and_30_out, and_31_out, not_1_out, not_2_out, not_3_out, not_4_out, not_5_out,
       not_6_out, not_7_out, not_8_out, not_9_out, not_10_out, not_11_out, not_12_out, not_13_out,
       not_14_out, not_15_out, not_16_out, not_17_out, not_18_out, not_19_out, not_20_out, not_21_out,
       not_22_out, not_23_out, not_24_out, not_25_out, not_26_out, not_27_out, not_28_out, not_29_out,
       not_30_out, not_31_out, not_32_out, not_33_out, not_34_out, not_35_out, not_36_out, not_37_out,
       not_38_out, not_39_out, or_1_out;
  wire [3:0] or_10_out, register_1_q;

  or or_1 (or_1_out, l7, true, dead);
  Register #(.width(4)) register_1 (.D(or_10_out), .Q(register_1_q), .clk(clock), .clr(clear));  // open: en
  not not_1 (not_1_out, register_1_q[3]);
  not not_2 (not_2_out, register_1_q[2]);
  not not_3 (not_3_out, register_1_q[1]);
  not not_4 (not_4_out, register_1_q[0]);
  not not_5 (not_5_out, register_1_q[3]);
  not not_6 (not_6_out, register_1_q[2]);
  not not_7 (not_7_out, register_1_q[1]);
  not not_8 (not_8_out, or_1_out);
  not not_9 (not_9_out, register_1_q[3]);
  not not_10 (not_10_out, register_1_q[2]);
  not not_11 (not_11_out, register_1_q[1]);
  not not_12 (not_12_out, register_1_q[0]);
  not not_13 (not_13_out, or_1_out);
  not not_14 (not_14_out, register_1_q[3]);
  not not_15 (not_15_out, register_1_q[2]);
  not not_16 (not_16_out, register_1_q[1]);
  not not_17 (not_17_out, register_1_q[0]);
  not not_18 (not_18_out, or_1_out);
  not not_19 (not_19_out, register_1_q[3]);
  and and_1 (and_1_out, not_19_out, register_1_q[1], or_1_out);
  and and_2 (and_2_out, register_1_q[2], or_1_out);
  and and_3 (and_3_out, register_1_q[3], not_20_out, or_1_out);
  not not_20 (not_20_out, register_1_q[1]);
  and and_4 (and_4_out, register_1_q[2], register_1_q[1]);
  and and_5 (and_5_out, register_1_q[2], not_21_out);
  not not_21 (not_21_out, register_1_q[1]);
  and and_6 (and_6_out, register_1_q[1], register_1_q[0]);
  and and_7 (and_7_out, register_1_q[2], register_1_q[0]);
  and and_8 (and_8_out, register_1_q[3], register_1_q[0]);
  and and_9 (and_9_out, register_1_q[3], register_1_q[1]);
  and and_10 (and_10_out, register_1_q[3], register_1_q[2]);
  and and_11 (and_11_out, register_1_q[2], register_1_q[1], register_1_q[0], or_1_out);
  not not_22 (not_22_out, register_1_q[3]);
  not not_23 (not_23_out, register_1_q[2]);
  not not_24 (not_24_out, register_1_q[3]);
  not not_25 (not_25_out, register_1_q[1]);
  not not_26 (not_26_out, register_1_q[3]);
  not not_27 (not_27_out, register_1_q[0]);
  not not_28 (not_28_out, register_1_q[3]);
  not not_29 (not_29_out, or_1_out);
  not not_30 (not_30_out, register_1_q[3]);
  not not_31 (not_31_out, register_1_q[2]);
  not not_32 (not_32_out, register_1_q[1]);
  not not_33 (not_33_out, register_1_q[1]);
  not not_34 (not_34_out, register_1_q[0]);
  not not_35 (not_35_out, or_1_out);
  not not_36 (not_36_out, register_1_q[0]);
  and and_12 (and_12_out, not_36_out, or_1_out);
  and and_13 (and_13_out, register_1_q[1], register_1_q[0], not_37_out);
  not not_37 (not_37_out, or_1_out);
  and and_14 (and_14_out, register_1_q[2], register_1_q[0], not_38_out);
  not not_38 (not_38_out, or_1_out);
  and and_15 (and_15_out, register_1_q[3], register_1_q[0], not_39_out);
  not not_39 (not_39_out, or_1_out);
  and and_16 (and_16_out, register_1_q[3], register_1_q[1], register_1_q[0]);
  and and_17 (and_17_out, register_1_q[3], register_1_q[2]);
  and and_18 (and_18_out, not_1_out, not_2_out, not_3_out, not_4_out);
  or or_2 (dec, and_18_out, and_19_out);
  and and_19 (and_19_out, not_5_out, not_6_out, not_7_out, not_8_out);
  and and_20 (\reg , not_9_out, not_10_out, not_11_out, not_12_out, not_13_out);
  and and_21 (letreg, not_14_out, not_15_out, not_16_out, not_17_out, not_18_out);
  or or_3 (regtty, and_1_out, and_2_out, and_3_out);
  or or_4 (cul2, and_4_out, register_1_q[3]);
  or or_5 (cu1, and_5_out, register_1_q[3]);
  or or_6 (cu0, and_6_out, and_7_out, and_8_out, and_9_out, and_10_out);
  or or_7 (or_10_out[3], and_11_out, register_1_q[3]);
  and and_22 (and_22_out, not_22_out, not_23_out, register_1_q[1], register_1_q[0], or_1_out);
  and and_23 (and_23_out, not_24_out, register_1_q[2], not_25_out);
  and and_24 (and_24_out, not_26_out, register_1_q[2], not_27_out);
  and and_25 (and_25_out, not_28_out, register_1_q[2], not_29_out);
  and and_26 (and_26_out, not_30_out, not_31_out, not_32_out, register_1_q[0]);
  and and_27 (and_27_out, not_33_out, register_1_q[0], or_1_out);
  and and_28 (and_28_out, register_1_q[1], not_34_out);
  and and_29 (and_29_out, register_1_q[1], not_35_out);
  and and_30 (and_30_out, register_1_q[3], register_1_q[1]);
  and and_31 (and_31_out, register_1_q[3], register_1_q[2]);
  or or_8 (or_10_out[2], and_22_out, and_23_out, and_24_out, and_25_out);
  or or_9 (or_10_out[1], and_26_out, and_27_out, and_28_out, and_29_out, and_30_out, and_31_out);
  or or_10 (or_10_out[0], and_12_out, and_13_out, and_14_out, and_15_out, and_16_out, and_17_out);
endmodule

module matris (
  input  F,
  input  clock,
  input  clear,
  output [6:0] N4,
  output [6:0] N3,
  output [6:0] N1,
  output dead,
  output [6:0] N2,
  output [6:0] N0
);

  wire and_1_out, and_2_out, and_3_out, and_4_out, and_5_out, and_6_out, and_7_out, and_8_out, and_9_out,
       and_10_out, and_11_out, and_14_out, and_15_out, and_16_out, and_17_out, and_18_out, and_19_out,
       and_20_out, and_21_out, and_22_out, and_23_out, and_24_out, and_25_out, and_26_out, and_27_out,
       not_1_out, not_2_out, not_3_out, not_4_out, not_5_out, not_6_out, not_7_out, not_8_out, not_9_out,
       not_10_out, not_11_out, not_12_out, not_13_out, not_14_out;
  wire [2:0] or_4_out;
  wire [3:0] register_1_q;

  and and_1 (and_1_out, register_1_q[2], register_1_q[1], register_1_q[0], F);
  not not_1 (not_1_out, register_1_q[2]);
  not not_2 (not_2_out, register_1_q[1]);
  not not_3 (not_3_out, register_1_q[0]);
  not not_4 (not_4_out, F);
  not not_5 (not_5_out, register_1_q[1]);
  not not_6 (not_6_out, register_1_q[0]);
  not not_7 (not_7_out, F);
  not not_8 (not_8_out, register_1_q[3]);
  not not_9 (not_9_out, register_1_q[0]);
  not not_10 (not_10_out, register_1_q[1]);
  not not_11 (not_11_out, register_1_q[0]);
  not not_12 (not_12_out, F);
  or or_1 (N0[3], and_1_out, register_1_q[3]);
  and and_2 (and_2_out, not_1_out, register_1_q[1], register_1_q[0], F);
  and and_3 (and_3_out, register_1_q[2], not_2_out);
  and and_4 (and_4_out, register_1_q[2], not_3_out);
  and and_5 (and_5_out, register_1_q[2], not_4_out);
  and and_6 (and_6_out, not_5_out, register_1_q[0], F);
  and and_7 (and_7_out, register_1_q[1], not_6_out);
  and and_8 (and_8_out, register_1_q[1], not_7_out);
  and and_9 (and_9_out, not_8_out, not_9_out, F);
  and and_10 (and_10_out, not_10_out, not_11_out, F);
  and and_11 (and_11_out, register_1_q[0], not_12_out);
  Register #(.width(4)) register_1 (.D({N0[3], or_4_out}), .Q(register_1_q), .clk(clock), .clr(clear));  // open: en
  or or_2 (or_4_out[2], and_2_out, and_3_out, and_4_out, and_5_out);
  or or_3 (or_4_out[1], and_6_out, and_7_out, and_8_out);
  or or_4 (or_4_out[0], and_9_out, and_10_out, and_11_out);
  not not_13 (not_13_out, or_4_out[0]);
  not not_14 (not_14_out, or_4_out[2]);
  and and_12 (N0[0], N0[3], or_4_out[1]);
  and and_13 (dead, not_13_out, or_4_out[1], not_14_out, N0[3]);
  or or_5 (N3[6], or_4_out[2], N0[3]);
  and and_14 (and_14_out, or_4_out[2], or_4_out[0]);
  or or_6 (N2[6], and_14_out, and_15_out, N0[3]);
  and and_15 (and_15_out, or_4_out[2], or_4_out[1]);
  and and_16 (and_16_out, or_4_out[2], or_4_out[1], or_4_out[0]);
  or or_7 (N2[3], and_16_out, N0[3]);
  and and_17 (and_17_out, N0[3], or_4_out[0]);
  or or_8 (N2[0], and_17_out, and_18_out);
  and and_18 (and_18_out, N0[3], or_4_out[1]);
  or or_9 (N4[6], or_4_out[2], N0[3]);
  and and_19 (and_19_out, or_4_out[1], or_4_out[0]);
  or or_10 (N4[5], and_19_out, or_4_out[2], N0[3]);
  and and_20 (and_20_out, or_4_out[1], or_4_out[0]);
  or or_11 (N4[4], and_20_out, or_4_out[2], N0[3]);
  or or_12 (N4[3], or_4_out[1], or_4_out[2], N0[3]);
  or or_13 (N4[2], or_4_out[1], or_4_out[2], N0[3]);
  or or_14 (N4[1], or_4_out[0], or_4_out[1], or_4_out[2], N0[3]);
  or or_15 (N4[0], or_4_out[0], or_4_out[1], or_4_out[2], N0[3]);
  and and_21 (and_21_out, or_4_out[2], or_4_out[0]);
  and and_22 (and_22_out, or_4_out[2], or_4_out[1]);
  and and_23 (and_23_out, or_4_out[2], or_4_out[1]);
  and and_24 (and_24_out, or_4_out[2], or_4_out[1]);
  and and_25 (and_25_out, or_4_out[2], or_4_out[1], or_4_out[0]);
  and and_26 (and_26_out, N0[3], or_4_out[0]);
  and and_27 (and_27_out, N0[3], or_4_out[1]);
  and and_28 (N1[0], N0[3], or_4_out[1]);
  or or_16 (N1[6], and_21_out, and_22_out, N0[3]);
  or or_17 (N1[5], and_23_out, N0[3]);
  or or_18 (N1[4], and_24_out, N0[3]);
  or or_19 (N1[3], and_25_out, N0[3]);
  or or_20 (N1[1], and_26_out, and_27_out);

  assign {N0[6:4], N0[2:1]} = {5{1'b0}};
  assign N1[2] = N0[3];
  assign {N2[5:4], N2[2:1]} = 4'b0000;
  assign N3[5:0] = {6{1'b0}};
endmodule

// false
module score_table (
  input  [2:0] Cu,
  input  fls,
  input  score_clear,
  input  clock,
  output [3:0] nuumber
);

  wire and_1_out, and_4_out, not_1_out, not_2_out, not_3_out, not_4_out;
  wire [1:0] and_2_out, register_1_q;

  not not_1 (not_1_out, fls);
  and and_1 (and_1_out, Cu[2], Cu[1], Cu[0], not_1_out);
  and and_2 (and_2_out[0], register_1_q[1], and_1_out);
  not not_2 (not_2_out, register_1_q[1]);
  not not_3 (not_3_out, register_1_q[1]);
  not not_4 (not_4_out, register_1_q[0]);
  and and_3 (and_2_out[1], not_2_out, and_1_out);
  and and_4 (and_4_out, not_3_out, not_4_out, and_1_out);
  Register #(.width(2)) register_1 (.D(and_2_out), .en(1'b1), .Q(register_1_q), .clk(clock));  // open: clr
  Counter #(.width(4), .max('hf)) counter_1 (
    .count(and_4_out), .Q(nuumber), .clk(clock), .clr(score_clear));  // open: load, D, carry
endmodule

module score_decoder (
  input  d,
  input  c,
  input  b,
  input  a,
  input  decoder_enable,
  input  clock,
  input  score_clear,
  output a_2,
  output b_2,
  output c_2,
  output d_2,
  output e,
  output f,
  output g
);

  wire and_1_out, and_2_out, and_3_out, and_4_out, and_5_out, and_6_out, and_7_out, and_8_out, and_9_out,
       and_10_out, and_11_out, and_12_out, and_13_out, and_14_out, and_15_out, and_16_out, not_1_out,
       not_2_out, not_3_out, not_4_out, not_5_out, not_6_out, not_7_out, not_8_out, not_9_out, not_10_out,
       not_11_out, not_12_out, not_13_out, not_14_out, not_15_out, not_16_out, not_17_out, not_18_out,
       not_19_out, not_20_out, not_21_out;
  wire [3:0] register_1_q;

  Register #(.width(4)) register_1 (
    .D({a, b, c, d}), .en(decoder_enable), .Q(register_1_q), .clk(clock), .clr(score_clear));
  not not_1 (not_1_out, register_1_q[1]);
  not not_2 (not_2_out, register_1_q[3]);
  not not_3 (not_3_out, register_1_q[2]);
  not not_4 (not_4_out, register_1_q[3]);
  not not_5 (not_5_out, register_1_q[2]);
  not not_6 (not_6_out, register_1_q[1]);
  not not_7 (not_7_out, register_1_q[3]);
  not not_8 (not_8_out, register_1_q[1]);
  not not_9 (not_9_out, register_1_q[3]);
  not not_10 (not_10_out, register_1_q[2]);
  not not_11 (not_11_out, register_1_q[1]);
  not not_12 (not_12_out, register_1_q[3]);
  not not_13 (not_13_out, register_1_q[3]);
  not not_14 (not_14_out, register_1_q[2]);
  not not_15 (not_15_out, register_1_q[3]);
  not not_16 (not_16_out, register_1_q[2]);
  not not_17 (not_17_out, register_1_q[3]);
  not not_18 (not_18_out, register_1_q[1]);
  not not_19 (not_19_out, register_1_q[2]);
  not not_20 (not_20_out, register_1_q[3]);
  and and_1 (and_1_out, not_1_out, not_2_out);
  and and_2 (and_2_out, register_1_q[1], register_1_q[3]);
  not not_21 (not_21_out, register_1_q[1]);
  and and_3 (and_3_out, not_3_out, not_4_out);
  and and_4 (and_4_out, register_1_q[2], register_1_q[3]);
  or or_1 (c_2, not_5_out, register_1_q[3], register_1_q[1]);
  and and_5 (and_5_out, not_6_out, not_7_out);
  and and_6 (and_6_out, not_8_out, register_1_q[2]);
  and and_7 (and_7_out, register_1_q[2], not_9_out);
  and and_8 (and_8_out, register_1_q[1], not_10_out, register_1_q[3]);
  and and_9 (and_9_out, not_11_out, not_12_out);
  and and_10 (and_10_out, register_1_q[2], not_13_out);
  and and_11 (and_11_out, not_14_out, not_15_out);
  and and_12 (and_12_out, register_1_q[1], not_16_out);
  and and_13 (and_13_out, register_1_q[1], not_17_out);
  and and_14 (and_14_out, not_18_out, register_1_q[2]);
  and and_15 (and_15_out, register_1_q[1], not_19_out);
  and and_16 (and_16_out, register_1_q[1], not_20_out);
  or or_2 (a_2, and_1_out, register_1_q[2], and_2_out, register_1_q[0]);
  or or_3 (b_2, not_21_out, and_3_out, and_4_out);
  or or_4 (d_2, and_5_out, and_6_out, and_7_out, and_8_out, register_1_q[0]);
  or or_5 (e, and_9_out, and_10_out);
  or or_6 (f, and_11_out, and_12_out, and_13_out, register_1_q[0]);
  or or_7 (g, and_14_out, and_15_out, and_16_out, register_1_q[0]);
endmodule

module rom (
  input  Clock,
  input  random_enable,
  output [7:0] N1,
  output [7:0] N2,
  output [7:0] N3,
  output [7:0] N4,
  output [7:0] N5,
  output [7:0] N6,
  output [7:0] N7,
  output [7:0] N8
);

  wire [6:0] random_1_out;

  Random #(.width(7)) random_1 (.clk(Clock), .next(random_enable), .out(random_1_out));  // open: clr
  ROM #(.addrWidth(7), .dataWidth(32)) rom_1 (.addr(random_1_out), .data({N5, N6, N7, N8}));  // open: sel
  ROM #(.addrWidth(7), .dataWidth(32)) rom_2 (.addr(random_1_out), .data({N1, N2, N3, N4}));  // open: sel

  // Notes on the sheet:
  //   contents of rom_1 (hex, n*v repeats v):
  //   5954484d 55494359 414e4e59 4f4e4943 4a555259 55495053 52555348 5a5a4553 4152545a 464f4f4e 53544943
  //   495a4d4f 41544348 45424f58 5947454e 5846554c 4e475448 55584f4d 58494f4d 4c494e47 544f574e 4f544943
  //   5341434b 534b4559 494c4348 415a5a59 5a45424f 4c465448 50504552 52564553 4958454c 41564f57 48594d45
  //   55434b59 52414745 4f434b59 544f4d53 53414c45 5946554c 43414c4c 5a415244 47544853 434b4559 48544841
  //   564f5259 4d414745 53534950 55495249 42595445 524e444c 43494e47 45504c59 4b494e47 4e4f574e 55455545
  //   52595054 414f5552 44415953 4e5a4950 59494e47 42424544 5a494e47 41524c59 4e455354 5a5a4c45 57415645
  //   5048454e 47494e47 414c545a 51554554 41524f4f 494d5059 47534157 5a415244 4a414d41 4b494553 46544853
  //   4f4c4b53 4b574159 4c49545a 55495245 52494445 42424544 57415859 5a4c4544 554d424f 51554950 54534348
  //   57415659 59434c45 54414646 574f524d 464f5254 46414c4f 4c55545a 5a494e47 45564552 574f524d 5a415244
  //   45424f58 48534941 45505448 57415244 4c595048 47474c45 45544348 5a555245 46494c4d 5a4c4544 4c4f5645
  //   51554953 504c4558 454c4c59 475a4147 554e4e59 54524958 41494b55 58434152 4a494e58 4846554c 41505053
  //   49424c59 554d4d59 454e5545 534b4557 52544859 45455a59 44495a45
  //   contents of rom_2 (hex, n*v repeats v):
  //   5248 4a 44 4d4e454d 494e 51 0 515549 5155 425546 474e4f 47 534352 4a554b 4f58 424f 53545245 42 41
  //   50555a5a 5550 51554958 4b4e4150 574849 5a 4a 4741 545745 5a49 445741 50 444953 52 4c 4741 52 435553
  //   0 4a4f 5245 5749 4c454e 4a4f 4e4150 49 4441 474f 44414951 4b494c4f 4449 4641 4445 4a4f 554e4b 51 43
  //   4749 4e4f5741 55 44495a5a 5255 5748495a 474e 4649 454d4245 0 4859 4a4f47 57 43524f 4255434b 57 4a49
  //   424c495a 5041 434f4f 5457454c 46 57414c 42 524551 50 475241 0 4652495a 4a 45 4b49 0 43 53 474c4f57 0
  //   425546 4b 42555a 57484f4d 424f4f4b 42555a 4943 465543 44 41574b 47 424f 535452 41 0 4652415a
  //   464f5847 4d4152 4455 4a 5a49 46 4d41 48 424f 0 594f5554 5343484e 504f5353 59 4156 41 554e574f 5748
  //   4f5849
endmodule
