// Logisim project 1320cpu.circ as structural Verilog: 1 circuit, main circuit main
module main (
  input  eq,
  input  gt,
  input  run,
  input  clock,
  input  clear,
  output S2,
  output S1,
  output S0,
  output go
);

  wire and_2_out, and_3_out, and_4_out, and_5_out, not_1_out, not_2_out, not_3_out, not_4_out, not_5_out,
       not_6_out, not_7_out, not_8_out, not_9_out;
  wire [2:0] register_1_q;

  Register #(.width(3)) register_1 (.D({S2, S1, S0}), .en(clock), .Q(register_1_q), .clk(clock), .clr(clear));
  and and_1 (S2, register_1_q[0], not_1_out);
  not not_1 (not_1_out, gt);
  not not_2 (not_2_out, register_1_q[2]);
  not not_3 (not_3_out, register_1_q[0]);
  and and_2 (and_2_out, not_2_out, not_3_out, run);
  and and_3 (and_3_out, register_1_q[0], not_4_out);
  not not_4 (not_4_out, eq);
  not not_5 (not_5_out, register_1_q[2]);
  not not_6 (not_6_out, register_1_q[0]);
  and and_4 (and_4_out, not_5_out, not_6_out, run);
  and and_5 (and_5_out, register_1_q[0], not_7_out);
  not not_7 (not_7_out, eq);
  not not_8 (not_8_out, register_1_q[2]);
  not not_9 (not_9_out, register_1_q[0]);
  and and_6 (go, not_8_out, not_9_out, run);
  or or_1 (S1, and_2_out, and_3_out);
  or or_2 (S0, and_4_out, and_5_out);
endmodule
