// Logisim project connected.circ as structural Verilog: 1 circuit, main circuit main
// start
module main (
  input  [15:0] a_input,
  input  Zero,
  input  [15:0] b_input,
  input  go,
  input  clear,
  input  [15:0] compare,
  input  [15:0] subs,
  output [15:0] Result,
  output [15:0] a_state_register,
  output [15:0] b_state_register
);

  wire clock_1_out, main_1_go, main_1_s0, main_1_s1, main_1_s2, main_2_eq, main_2_gt;

  Clock clock_1 (.out(clock_1_out));
  _1320cpu_main main_1 (
    .eq(main_2_eq), .gt(main_2_gt), .run(go), .clock(clock_1_out), .clear(clear), .S2(main_1_s2),
    .S1(main_1_s1), .S0(main_1_s0), .go(main_1_go));
  datapathson_main main_2 (
    .zero(Zero), .subin_0(Zero), .S0(main_1_s0), .A(a_input), .compare(compare), .subs(subs), .B(b_input),
    .go(main_1_go), .clock(clock_1_out), .zero1(Zero), .S1(main_1_s1), .s2(main_1_s2), .clear(clear),
    .res(Result), .gt(main_2_gt), .eq(main_2_eq), .a_statte_pin(a_state_register), .adin_0(Zero),
    .b_state(b_state_register));

  // Notes on the sheet:
  //   *Clear pin is for restart
  //   Controll Unit
  //   *Number is input than 'go' pin do 1   
  //   * İf calculate multipication than press clear 
  //   *user can calculate negatif number
  //   Datapath
  //   !!!WARNİNG!!! 
  //   you should make subs '1' before start program
endmodule
