// Logisim project datapathson.circ as structural Verilog: 1 circuit, main circuit main
module main (
  input  zero,
  input  subin_0,
  input  S0,
  input  [15:0] A,
  input  [15:0] compare,
  input  adin_0,
  input  [15:0] subs,
  input  [15:0] B,
  input  go,
  input  clock,
  input  zero1,
  input  S1,
  input  s2,
  input  clear,
  output [15:0] res,
  output gt,
  output eq,
  output [15:0] a_statte_pin,
  output [15:0] b_state
);

  wire comparator_1_lt, subtractor_1_bout;
  wire [15:0] adder_1_out, multiplexer_1_out, subtractor_1_out;
  wire [15:15] and_1_out, and_2_out, register_1_q;

  and and_1 (and_1_out[15], zero, A[15]);
  and and_2 (and_2_out[15], zero1, B[15]);
  xor xor_1 (res[15], B[15], A[15]);
  Register #(.width(16)) a_state (.D(multiplexer_1_out), .en(S0), .Q(a_statte_pin), .clk(clock), .clr(clear));
  Multiplexer #(.width(16), .enable("false")) multiplexer_1 (
    .in0(subtractor_1_out), .in1({and_1_out[15], A[14:0]}), .out(multiplexer_1_out), .sel(go));
  Register #(.width(16)) u_b_state (.D(adder_1_out), .en(S1), .Q(b_state), .clk(clock), .clr(clear));
  Subtractor #(.width(16)) subtractor_1 (
    .a(a_statte_pin), .b(subs), .out(subtractor_1_out), .bin(subin_0), .bout(subtractor_1_bout));
  Comparator #(.width(16)) comparator_1 (.a(subtractor_1_out), .b(compare), .gt(gt), .eq(eq), .lt(comparator_1_lt));
  Adder #(.width(16)) adder_1 (
    .a({and_2_out[15], B[14:0]}), .b(b_state), .out(adder_1_out), .cin(adin_0));  // open: cout
  Register #(.width(16)) register_1 (.D(b_state), .en(s2), .Q({register_1_q[15], res[14:0]}), .clk(clock), .clr(clear));

  // Notes on the sheet:
  //   res: pull=down
  //   negative number convert to positive
  //   -x-=+  -x+=-  xor is convert number
  //   for negatif number
  //   for negatif number
  //   make '1' before start 
  //   Result
endmodule
