// Logisim project 171044073.circ as structural Verilog: 3 circuits, main circuit main
module main (
);

  wire buton1_out, buton2_out, clock_1_out, decoder_display_1_a_2, decoder_display_1_b_2,
       decoder_display_1_c_2, decoder_display_1_d_2, decoder_display_1_e, decoder_display_1_f,
       decoder_display_1_g, decoder_display_2_a_2, decoder_display_2_b_2, decoder_display_2_c_2,
       decoder_display_2_d_2, decoder_display_2_e, decoder_display_2_f, decoder_display_2_g, display2_1_s0,
       display2_1_s1, display2_1_s2, display2_1_s3, display2_2_s0, display2_2_s1, display2_2_s2,
       display2_2_s3, main_1_l1, main_1_l2, main_1_l3, main_1_l4, main_1_l5, main_1_l6, main_1_l7, reset_out;

  Button buton1 (.out(buton1_out));
  Button buton2 (.out(buton2_out));
  Clock clock_1 (.out(clock_1_out));
  Button reset (.out(reset_out));
  proje_main main_1 (
    .b1(buton1_out), .clock(clock_1_out), .r(reset_out), .b2(buton2_out), .L1(main_1_l1), .L2(main_1_l2),
    .L3(main_1_l3), .L4(main_1_l4), .L5(main_1_l5), .L6(main_1_l6), .L7(main_1_l7));
  LED led1 (.in(main_1_l1));
  LED led2 (.in(main_1_l2));
  LED led3 (.in(main_1_l3));
  LED led4 (.in(main_1_l4));
  LED led5 (.in(main_1_l5));
  LED led6 (.in(main_1_l6));
  LED led7 (.in(main_1_l7));
  decoder_display decoder_display_1 (
    .D(display2_1_s3), .C(display2_1_s2), .B(display2_1_s1), .A(display2_1_s0), .a_2(decoder_display_1_a_2),
    .b_2(decoder_display_1_b_2), .c_2(decoder_display_1_c_2), .d_2(decoder_display_1_d_2),
    .e(decoder_display_1_e), .f(decoder_display_1_f), .g(decoder_display_1_g));
  display2 display2_1 (
    .b1(1'b0), .led1(main_1_l1), .clock(clock_1_out), .s3(display2_1_s3), .s2(display2_1_s2),
    .s1(display2_1_s1), .s0(display2_1_s0));
  decoder_display decoder_display_2 (
    .D(display2_2_s3), .C(display2_2_s2), .B(display2_2_s1), .A(display2_2_s0), .a_2(decoder_display_2_a_2),
    .b_2(decoder_display_2_b_2), .c_2(decoder_display_2_c_2), .d_2(decoder_display_2_d_2),
    .e(decoder_display_2_e), .f(decoder_display_2_f), .g(decoder_display_2_g));
  display2 display2_2 (
    .b1(1'b0), .led1(main_1_l7), .clock(clock_1_out), .s3(display2_2_s3), .s2(display2_2_s2),
    .s1(display2_2_s1), .s0(display2_2_s0));
  _7_Segment_Display u_7_segment_display_1 (
    .g(decoder_display_1_g), .f(decoder_display_1_f), .a(decoder_display_1_a_2), .b(decoder_display_1_b_2),
    .e(decoder_display_1_e), .d(decoder_display_1_d_2), .c(decoder_display_1_c_2));  // open: dp
  _7_Segment_Display u_7_segment_display_2 (
    .g(decoder_display_2_g), .f(decoder_display_2_f), .a(decoder_display_2_a_2), .b(decoder_display_2_b_2),
    .e(decoder_display_2_e), .d(decoder_display_2_d_2), .c(decoder_display_2_c_2));  // open: dp

  // Notes on the sheet:
  //   not press buton long time , if press button long time button aoutput is 0  
endmodule

module decoder_display (
  input  D,
  input  C,
  input  B,
  input  A,
  output a_2,
  output b_2,
  output c_2,
  output d_2,
  output e,
  output f,
  output g
);

  wire and_1_out, and_2_out, and_3_out, and_4_out, and_5_out, and_6_out, and_7_out, and_8_out, and_9_out,
       and_10_out, and_11_out, and_12_out, and_13_out, and_14_out, and_15_out, and_16_out, not_1_out,
       not_2_out, not_3_out, not_4_out, not_5_out, not_6_out, not_7_out, not_8_out, not_9_out, not_10_out,
       not_11_out, not_12_out, not_13_out, not_14_out, not_15_out, not_16_out, not_17_out, not_18_out,
       not_19_out, not_20_out, not_21_out;

  not not_1 (not_1_out, C);
  and and_1 (and_1_out, not_1_out, not_2_out);
  not not_2 (not_2_out, A);
  and and_2 (and_2_out, C, A);
  not not_3 (not_3_out, C);
  not not_4 (not_4_out, B);
  and and_3 (and_3_out, not_4_out, not_5_out);
  not not_5 (not_5_out, A);
  and and_4 (and_4_out, B, A);
  not not_6 (not_6_out, B);
  or or_1 (c_2, not_6_out, A, C);
  not not_7 (not_7_out, C);
  and and_5 (and_5_out, not_7_out, not_8_out);
  not not_8 (not_8_out, A);
  not not_9 (not_9_out, C);
  and and_6 (and_6_out, not_9_out, B);
  and and_7 (and_7_out, B, not_10_out);
  not not_10 (not_10_out, A);
  not not_11 (not_11_out, B);
  and and_8 (and_8_out, C, not_11_out, A);
  not not_12 (not_12_out, C);
  and and_9 (and_9_out, not_12_out, not_13_out);
  not not_13 (not_13_out, A);
  and and_10 (and_10_out, B, not_14_out);
  not not_14 (not_14_out, A);
  not not_15 (not_15_out, B);
  and and_11 (and_11_out, not_15_out, not_16_out);
  not not_16 (not_16_out, A);
  and and_12 (and_12_out, C, not_17_out);
  not not_17 (not_17_out, B);
  and and_13 (and_13_out, C, not_18_out);
  not not_18 (not_18_out, A);
  not not_19 (not_19_out, C);
  and and_14 (and_14_out, not_19_out, B);
  and and_15 (and_15_out, C, not_20_out);
  not not_20 (not_20_out, B);
  and and_16 (and_16_out, C, not_21_out);
  not not_21 (not_21_out, A);
  or or_2 (a_2, and_1_out, B, and_2_out, D);
  or or_3 (b_2, not_3_out, and_3_out, and_4_out);
  or or_4 (d_2, and_5_out, and_6_out, and_7_out, and_8_out, D);
  or or_5 (e, and_9_out, and_10_out);
  or or_6 (f, and_11_out, and_12_out, and_13_out, D);
  or or_7 (g, and_14_out, and_15_out, and_16_out, D);
endmodule

module display2 (
  input  b1,
  input  led1,
  input  clock,
  output s3,
  output s2,
  output s1,
  output s0
);

  wire and_3_out, and_4_out, and_5_out, and_6_out, and_7_out, and_8_out, and_9_out, and_10_out, and_11_out,
       and_12_out, and_13_out, and_14_out, and_15_out, and_16_out, and_17_out, and_18_out, and_19_out,
       and_20_out, and_21_out, and_22_out, and_23_out, and_24_out, and_25_out, not_1_out, not_2_out,
       not_3_out, not_4_out, not_5_out, not_6_out, not_7_out, not_8_out, not_9_out, not_10_out, not_11_out,
       not_12_out, not_13_out, not_14_out, not_15_out, not_16_out, not_17_out, not_18_out, not_19_out,
       not_20_out, not_21_out, not_22_out, not_23_out, not_24_out, not_25_out, not_26_out, not_27_out,
       not_28_out;
  wire [1:0] and_1_out, register_1_q;
  wire [3:0] or_4_out, register_2_q;

  and and_1 (and_1_out[0], register_1_q[1], led1);
  not not_1 (not_1_out, register_1_q[1]);
  not not_2 (not_2_out, register_1_q[1]);
  not not_3 (not_3_out, register_1_q[0]);
  and and_2 (and_1_out[1], not_1_out, led1);
  and and_3 (and_3_out, not_2_out, not_3_out, led1);
  Register #(.width(2)) register_1 (.D(and_1_out), .en(1'b1), .Q(register_1_q), .clk(clock));  // open: clr
  Register #(.width(4)) register_2 (.D(or_4_out), .en(1'b1), .Q(register_2_q), .clk(and_3_out));  // open: clr
  and and_4 (and_4_out, register_2_q[1], register_2_q[2], register_2_q[3], b1);
  not not_4 (not_4_out, register_2_q[1]);
  not not_5 (not_5_out, register_2_q[2]);
  not not_6 (not_6_out, register_2_q[3]);
  not not_7 (not_7_out, b1);
  not not_8 (not_8_out, register_2_q[2]);
  and and_5 (and_5_out, not_8_out, register_2_q[3], b1);
  and and_6 (and_6_out, register_2_q[2], not_9_out);
  not not_9 (not_9_out, register_2_q[3]);
  and and_7 (and_7_out, register_2_q[2], not_10_out);
  not not_10 (not_10_out, b1);
  not not_11 (not_11_out, register_2_q[3]);
  and and_8 (and_8_out, not_11_out, b1);
  and and_9 (and_9_out, register_2_q[3], not_12_out);
  not not_12 (not_12_out, b1);
  not not_13 (not_13_out, register_2_q[3]);
  not not_14 (not_14_out, b1);
  not not_15 (not_15_out, register_2_q[1]);
  and and_10 (and_10_out, not_15_out, register_2_q[2], b1);
  not not_16 (not_16_out, register_2_q[1]);
  and and_11 (and_11_out, not_16_out, register_2_q[2], register_2_q[3]);
  and and_12 (and_12_out, register_2_q[1], not_17_out);
  not not_17 (not_17_out, register_2_q[2]);
  not not_18 (not_18_out, register_2_q[3]);
  and and_13 (and_13_out, register_2_q[1], not_18_out, not_19_out);
  not not_19 (not_19_out, b1);
  not not_20 (not_20_out, register_2_q[2]);
  and and_14 (and_14_out, not_20_out, b1);
  not not_21 (not_21_out, register_2_q[2]);
  and and_15 (and_15_out, not_21_out, register_2_q[3]);
  and and_16 (and_16_out, register_2_q[2], not_22_out, not_23_out);
  not not_22 (not_22_out, register_2_q[3]);
  not not_23 (not_23_out, b1);
  not not_24 (not_24_out, register_2_q[0]);
  and and_17 (and_17_out, not_24_out, not_25_out, not_26_out);
  not not_25 (not_25_out, register_2_q[3]);
  not not_26 (not_26_out, b1);
  not not_27 (not_27_out, register_2_q[1]);
  and and_18 (and_18_out, not_27_out, register_2_q[3], b1);
  not not_28 (not_28_out, register_2_q[2]);
  and and_19 (and_19_out, not_28_out, register_2_q[3], b1);
  or or_1 (s3, and_4_out, register_2_q[0]);
  and and_20 (and_20_out, not_4_out, register_2_q[2], register_2_q[3], b1);
  and and_21 (and_21_out, register_2_q[1], not_5_out);
  and and_22 (and_22_out, register_2_q[1], not_6_out);
  and and_23 (and_23_out, register_2_q[1], not_7_out);
  or or_2 (s1, and_5_out, and_6_out, and_7_out);
  or or_3 (s0, and_8_out, and_9_out);
  and and_24 (and_24_out, register_2_q[1], register_2_q[2], not_13_out, b1);
  or or_4 (or_4_out[0], and_24_out, and_25_out);
  and and_25 (and_25_out, register_2_q[1], register_2_q[2], register_2_q[3], not_14_out);
  or or_5 (or_4_out[1], and_10_out, and_11_out, and_12_out, and_13_out);
  or or_6 (or_4_out[2], and_14_out, and_15_out, and_16_out);
  or or_7 (or_4_out[3], and_17_out, and_18_out, and_19_out);
  or or_8 (s2, and_20_out, and_21_out, and_22_out, and_23_out);
endmodule
