// Logisim project proje.circ as structural Verilog: 1 circuit, main circuit main
module main (
  input  b1,
  input  clock,
  input  r,
  input  b2,
  output L1,
  output L2,
  output L3,
  output L4,
  output L5,
  output L6,
  output L7
);

  wire and_4_out, and_6_out, and_7_out, and_8_out, and_9_out, and_10_out, and_11_out, and_12_out, and_13_out,
       and_14_out, and_15_out, and_16_out, and_17_out, and_18_out, and_19_out, and_20_out, and_21_out,
       and_22_out, and_23_out, and_24_out, and_25_out, and_26_out, and_27_out, and_28_out, and_29_out,
       and_30_out, and_31_out, and_32_out, and_33_out, and_34_out, and_35_out, and_36_out, and_37_out,
       and_38_out, and_39_out, and_40_out, and_41_out, and_42_out, and_43_out, and_44_out, and_45_out,
       and_46_out, not_1_out, not_2_out, not_3_out, not_4_out, not_5_out, not_6_out, not_7_out, not_8_out,
       not_9_out, not_10_out, not_11_out, not_12_out, not_13_out, not_14_out, not_15_out, not_16_out,
       not_17_out, not_18_out, not_19_out, not_20_out, not_21_out, not_22_out, not_23_out, not_24_out,
       not_25_out, not_26_out, not_27_out, not_28_out, not_29_out, not_30_out, not_31_out, not_32_out,
       not_33_out, not_34_out, not_35_out, not_36_out, not_37_out, not_38_out, not_39_out, not_40_out,
       not_41_out, not_42_out, not_43_out, not_44_out, not_45_out, not_46_out, not_47_out, not_48_out,
       not_49_out, not_50_out, not_51_out, not_52_out, not_53_out, not_54_out, not_55_out, not_56_out,
       not_57_out, not_58_out, not_59_out, not_60_out, not_61_out, not_62_out, not_63_out, not_64_out,
       not_65_out, not_66_out, not_67_out, not_68_out, not_69_out, not_70_out, not_71_out, not_72_out,
       not_73_out, not_74_out, not_75_out, not_76_out, not_77_out, not_78_out, not_79_out, not_80_out,
       not_81_out, not_82_out, not_83_out, not_84_out, not_85_out, not_86_out, not_87_out, not_88_out,
       not_89_out, not_90_out, not_91_out, not_92_out, not_93_out, not_94_out, not_95_out, not_96_out,
       not_97_out, not_98_out, not_99_out, not_100_out, not_101_out, not_102_out, not_103_out, not_104_out,
       not_105_out, not_106_out, not_107_out, not_108_out, not_109_out, not_110_out, not_111_out,
       not_112_out, not_113_out, not_114_out;
  wire [1:0] and_1_out, and_2_out, register_1_q, register_2_q;
  wire [2:0] or_8_out, register_3_q;

  and and_1 (and_1_out[0], register_2_q[1], b1);
  not not_1 (not_1_out, register_2_q[1]);
  not not_2 (not_2_out, register_2_q[1]);
  not not_3 (not_3_out, register_2_q[0]);
  and and_2 (and_2_out[0], register_1_q[1], b2);
  not not_4 (not_4_out, register_1_q[1]);
  and and_3 (and_2_out[1], not_4_out, b2);
  not not_5 (not_5_out, register_1_q[1]);
  and and_4 (and_4_out, not_5_out, not_6_out, b2);
  not not_6 (not_6_out, register_1_q[0]);
  and and_5 (and_1_out[1], not_1_out, b1);
  and and_6 (and_6_out, not_2_out, not_3_out, b1);
  Register #(.width(2)) register_1 (.D(and_2_out), .en(1'b1), .Q(register_1_q), .clk(clock));  // open: clr
  Register #(.width(2)) register_2 (.D(and_1_out), .en(1'b1), .Q(register_2_q), .clk(clock));  // open: clr
  Register #(.width(3)) register_3 (.D(or_8_out), .en(1'b1), .Q(register_3_q), .clk(clock));  // open: clr
  not not_7 (not_7_out, register_3_q[0]);
  not not_8 (not_8_out, and_4_out);
  not not_9 (not_9_out, r);
  not not_10 (not_10_out, r);
  not not_11 (not_11_out, register_3_q[0]);
  not not_12 (not_12_out, register_3_q[1]);
  not not_13 (not_13_out, and_4_out);
  not not_14 (not_14_out, r);
  not not_15 (not_15_out, register_3_q[0]);
  not not_16 (not_16_out, register_3_q[2]);
  not not_17 (not_17_out, and_6_out);
  not not_18 (not_18_out, and_4_out);
  not not_19 (not_19_out, r);
  not not_20 (not_20_out, register_3_q[0]);
  not not_21 (not_21_out, register_3_q[2]);
  not not_22 (not_22_out, r);
  not not_23 (not_23_out, register_3_q[0]);
  not not_24 (not_24_out, register_3_q[1]);
  not not_25 (not_25_out, register_3_q[2]);
  not not_26 (not_26_out, and_4_out);
  not not_27 (not_27_out, r);
  not not_28 (not_28_out, register_3_q[0]);
  not not_29 (not_29_out, register_3_q[1]);
  not not_30 (not_30_out, and_6_out);
  not not_31 (not_31_out, and_4_out);
  not not_32 (not_32_out, r);
  not not_33 (not_33_out, register_3_q[0]);
  not not_34 (not_34_out, register_3_q[1]);
  not not_35 (not_35_out, r);
  not not_36 (not_36_out, register_3_q[0]);
  not not_37 (not_37_out, register_3_q[2]);
  not not_38 (not_38_out, and_6_out);
  not not_39 (not_39_out, r);
  not not_40 (not_40_out, register_3_q[0]);
  not not_41 (not_41_out, register_3_q[1]);
  not not_42 (not_42_out, register_3_q[2]);
  not not_43 (not_43_out, and_6_out);
  not not_44 (not_44_out, and_4_out);
  not not_45 (not_45_out, register_3_q[0]);
  not not_46 (not_46_out, register_3_q[1]);
  not not_47 (not_47_out, register_3_q[2]);
  not not_48 (not_48_out, register_3_q[0]);
  not not_49 (not_49_out, register_3_q[1]);
  not not_50 (not_50_out, and_6_out);
  not not_51 (not_51_out, register_3_q[1]);
  not not_52 (not_52_out, register_3_q[2]);
  not not_53 (not_53_out, and_4_out);
  not not_54 (not_54_out, register_3_q[0]);
  not not_55 (not_55_out, register_3_q[1]);
  not not_56 (not_56_out, register_3_q[2]);
  not not_57 (not_57_out, and_6_out);
  not not_58 (not_58_out, r);
  not not_59 (not_59_out, register_3_q[1]);
  not not_60 (not_60_out, register_3_q[2]);
  not not_61 (not_61_out, and_6_out);
  not not_62 (not_62_out, and_4_out);
  not not_63 (not_63_out, r);
  not not_64 (not_64_out, register_3_q[1]);
  not not_65 (not_65_out, register_3_q[2]);
  not not_66 (not_66_out, r);
  not not_67 (not_67_out, and_4_out);
  not not_68 (not_68_out, r);
  not not_69 (not_69_out, register_3_q[1]);
  not not_70 (not_70_out, register_3_q[2]);
  not not_71 (not_71_out, and_6_out);
  not not_72 (not_72_out, r);
  not not_73 (not_73_out, and_6_out);
  not not_74 (not_74_out, and_4_out);
  not not_75 (not_75_out, r);
  not not_76 (not_76_out, r);
  not not_77 (not_77_out, and_6_out);
  not not_78 (not_78_out, r);
  not not_79 (not_79_out, r);
  not not_80 (not_80_out, register_3_q[1]);
  not not_81 (not_81_out, register_3_q[2]);
  not not_82 (not_82_out, and_6_out);
  not not_83 (not_83_out, r);
  not not_84 (not_84_out, and_6_out);
  not not_85 (not_85_out, r);
  not not_86 (not_86_out, r);
  not not_87 (not_87_out, r);
  not not_88 (not_88_out, r);
  not not_89 (not_89_out, register_3_q[0]);
  not not_90 (not_90_out, and_4_out);
  not not_91 (not_91_out, r);
  not not_92 (not_92_out, and_4_out);
  not not_93 (not_93_out, r);
  not not_94 (not_94_out, r);
  not not_95 (not_95_out, r);
  not not_96 (not_96_out, and_6_out);
  not not_97 (not_97_out, r);
  not not_98 (not_98_out, r);
  not not_99 (not_99_out, register_3_q[0]);
  not not_100 (not_100_out, register_3_q[2]);
  not not_101 (not_101_out, and_4_out);
  not not_102 (not_102_out, r);
  not not_103 (not_103_out, and_6_out);
  not not_104 (not_104_out, and_4_out);
  not not_105 (not_105_out, r);
  not not_106 (not_106_out, r);
  not not_107 (not_107_out, register_3_q[0]);
  not not_108 (not_108_out, and_6_out);
  not not_109 (not_109_out, r);
  not not_110 (not_110_out, r);
  not not_111 (not_111_out, register_3_q[1]);
  not not_112 (not_112_out, register_3_q[2]);
  not not_113 (not_113_out, and_6_out);
  not not_114 (not_114_out, r);
  and and_7 (and_7_out, not_7_out, register_3_q[1], and_6_out, not_8_out, not_9_out);
  and and_8 (and_8_out, register_3_q[1], register_3_q[2], not_10_out);
  and and_9 (and_9_out, not_11_out, not_12_out, register_3_q[2], and_6_out, not_13_out, not_14_out);
  and and_10 (and_10_out, not_15_out, register_3_q[1], not_16_out, not_17_out, not_18_out, not_19_out);
  and and_11 (and_11_out, not_20_out, register_3_q[1], not_21_out, and_6_out, and_4_out, not_22_out);
  and and_12 (and_12_out, not_23_out, not_24_out, not_25_out, and_6_out, not_26_out, not_27_out);
  and and_13 (and_13_out, not_28_out, not_29_out, register_3_q[2], not_30_out, not_31_out, not_32_out);
  and and_14 (and_14_out, not_33_out, not_34_out, register_3_q[2], and_6_out, and_4_out, not_35_out);
  and and_15 (and_15_out, not_36_out, register_3_q[1], not_37_out, not_38_out, and_4_out, not_39_out);
  and and_16 (and_16_out, not_40_out, not_41_out, not_42_out, not_43_out, not_44_out);
  and and_17 (and_17_out, not_45_out, not_46_out, not_47_out, and_6_out, and_4_out);
  and and_18 (and_18_out, not_48_out, not_49_out, register_3_q[2], not_50_out, and_4_out);
  and and_19 (and_19_out, register_3_q[0], not_51_out, not_52_out, and_6_out, not_53_out);
  and and_20 (and_20_out, not_54_out, not_55_out, not_56_out, not_57_out, and_4_out, not_58_out);
  and and_21 (and_21_out, register_3_q[0], not_59_out, not_60_out, not_61_out, not_62_out, not_63_out);
  and and_22 (and_22_out, register_3_q[0], not_64_out, not_65_out, and_6_out, and_4_out, not_66_out);
  and and_23 (and_23_out, register_3_q[0], register_3_q[2], and_6_out, not_67_out, not_68_out);
  and and_24 (and_24_out, register_3_q[0], not_69_out, not_70_out, not_71_out, and_4_out, not_72_out);
  and and_25 (and_25_out, register_3_q[0], register_3_q[2], not_73_out, not_74_out, not_75_out);
  and and_26 (and_26_out, register_3_q[0], register_3_q[2], and_6_out, and_4_out, not_76_out);
  and and_27 (and_27_out, register_3_q[0], register_3_q[2], not_77_out, and_4_out, not_78_out);
  and and_28 (and_28_out, register_3_q[0], register_3_q[1], not_79_out);
  and and_29 (and_29_out, not_80_out, not_81_out, not_82_out, and_4_out, not_83_out);
  and and_30 (and_30_out, register_3_q[0], not_84_out, not_85_out);
  and and_31 (and_31_out, register_3_q[0], and_4_out, not_86_out);
  and and_32 (and_32_out, register_3_q[0], register_3_q[2], not_87_out);
  and and_33 (and_33_out, register_3_q[0], register_3_q[1], not_88_out);
  and and_34 (and_34_out, register_3_q[0], register_3_q[1], and_6_out, and_4_out);
  and and_35 (and_35_out, not_89_out, register_3_q[2], and_6_out, not_90_out, not_91_out);
  and and_36 (and_36_out, register_3_q[1], not_92_out, not_93_out);
  and and_37 (and_37_out, register_3_q[1], and_6_out, not_94_out);
  and and_38 (and_38_out, register_3_q[1], register_3_q[2], not_95_out);
  and and_39 (and_39_out, register_3_q[0], register_3_q[2], not_96_out, and_4_out, not_97_out);
  and and_40 (and_40_out, register_3_q[0], register_3_q[1], not_98_out);
  and and_41 (and_41_out, not_99_out, not_100_out, and_6_out, not_101_out, not_102_out);
  and and_42 (and_42_out, register_3_q[2], not_103_out, not_104_out, not_105_out);
  and and_43 (and_43_out, register_3_q[2], and_6_out, and_4_out, not_106_out);
  and and_44 (and_44_out, not_107_out, register_3_q[1], not_108_out, and_4_out, not_109_out);
  and and_45 (and_45_out, register_3_q[1], register_3_q[2], not_110_out);
  and and_46 (and_46_out, register_3_q[0], not_111_out, not_112_out, not_113_out, and_4_out, not_114_out);
  or or_1 (L1, and_7_out, and_8_out);
  or or_2 (L2, and_9_out, and_10_out, and_11_out);
  or or_3 (L3, and_12_out, and_13_out, and_14_out, and_15_out);
  or or_4 (L4, and_16_out, r, and_17_out, and_18_out, and_19_out);
  or or_5 (L5, and_20_out, and_21_out, and_22_out, and_23_out);
  or or_6 (L6, and_24_out, and_25_out, and_26_out);
  or or_7 (L7, and_27_out, and_28_out);
  or or_8 (or_8_out[0], and_29_out, and_30_out, and_31_out, and_32_out, and_33_out, and_34_out);
  or or_9 (or_8_out[1], and_35_out, and_36_out, and_37_out, and_38_out, and_39_out, and_40_out);
  or or_10 (or_8_out[2], and_41_out, and_42_out, and_43_out, and_44_out, and_45_out, and_46_out);
endmodule
